// Logisim project ALU_project1.circ as structural Verilog: 4 circuits, main circuit 1b ALU 
module _1b_ALU (
  input  Cin,
  input  A_prime,
  input  [1:0] Op,
  input  A,
  input  B_prime,
  input  B,
  input  Less,
  output out_8,
  output Cout,
  output Set
);

  wire and_1_out, multiplexer_1_out, multiplexer_2_out, not_1_out, not_2_out, or_1_out;

  Multiplexer #(.enable("false")) multiplexer_1 (.in0(A), .in1(not_1_out), .out(multiplexer_1_out), .sel(A_prime));
  not not_1 (not_1_out, A);
  Multiplexer #(.enable("false")) multiplexer_2 (.in0(B), .in1(not_2_out), .out(multiplexer_2_out), .sel(B_prime));
  not not_2 (not_2_out, B);
  or or_1 (or_1_out, multiplexer_1_out, multiplexer_2_out);
  Adder #(.width(1)) adder_1 (.a(multiplexer_1_out), .b(multiplexer_2_out), .out(Set), .cin(Cin), .cout(Cout));
  and and_1 (and_1_out, multiplexer_1_out, multiplexer_2_out);
  Multiplexer #(.select(2), .enable("false")) multiplexer_3 (
    .in0(and_1_out), .in1(or_1_out), .in2(Set), .in3(Less), .out(out_8), .sel(Op));
endmodule

module ALU (
  input  Cin,
  input  A_prime,
  input  [15:0] B,
  input  [15:0] A,
  input  [1:0] Op,
  input  B_prime,
  output [15:0] out_7,
  output Zero
);

  wire n1b_alu_1_cout, n1b_alu_2_cout, n1b_alu_3_cout, n1b_alu_4_cout, n1b_alu_5_cout, n1b_alu_6_cout,
       n1b_alu_7_cout, n1b_alu_8_cout, n1b_alu_9_cout, n1b_alu_10_cout, n1b_alu_11_cout, n1b_alu_12_cout,
       n1b_alu_13_cout, n1b_alu_14_cout, n1b_alu_15_cout, n1b_alu_16_set;

  _1b_ALU u_1b_alu_1 (
    .A(A[0]), .B(B[0]), .Less(n1b_alu_16_set), .Cin(Cin), .Op(Op), .Cout(n1b_alu_1_cout), .A_prime(A_prime),
    .B_prime(B_prime), .out_8(out_7[0]));  // open: Set
  _1b_ALU u_1b_alu_2 (
    .A(A[1]), .B(B[1]), .Less(1'b0), .Cin(n1b_alu_1_cout), .Op(Op), .Cout(n1b_alu_2_cout), .A_prime(A_prime),
    .B_prime(B_prime), .out_8(out_7[1]));  // open: Set
  _1b_ALU u_1b_alu_3 (
    .A(A[2]), .B(B[2]), .Less(1'b0), .Cin(n1b_alu_2_cout), .Op(Op), .Cout(n1b_alu_3_cout), .A_prime(A_prime),
    .B_prime(B_prime), .out_8(out_7[2]));  // open: Set
  _1b_ALU u_1b_alu_4 (
    .A(A[3]), .B(B[3]), .Less(1'b0), .Cin(n1b_alu_3_cout), .Op(Op), .Cout(n1b_alu_4_cout), .A_prime(A_prime),
    .B_prime(B_prime), .out_8(out_7[3]));  // open: Set
  _1b_ALU u_1b_alu_5 (
    .A(A[4]), .B(B[4]), .Less(1'b0), .Cin(n1b_alu_4_cout), .Op(Op), .Cout(n1b_alu_5_cout), .A_prime(A_prime),
    .B_prime(B_prime), .out_8(out_7[4]));  // open: Set
  _1b_ALU u_1b_alu_6 (
    .A(A[5]), .B(B[5]), .Less(1'b0), .Cin(n1b_alu_5_cout), .Op(Op), .Cout(n1b_alu_6_cout), .A_prime(A_prime),
    .B_prime(B_prime), .out_8(out_7[5]));  // open: Set
  _1b_ALU u_1b_alu_7 (
    .A(A[6]), .B(B[6]), .Less(1'b0), .Cin(n1b_alu_6_cout), .Op(Op), .Cout(n1b_alu_7_cout), .A_prime(A_prime),
    .B_prime(B_prime), .out_8(out_7[6]));  // open: Set
  _1b_ALU u_1b_alu_8 (
    .A(A[7]), .B(B[7]), .Less(1'b0), .Cin(n1b_alu_7_cout), .Op(Op), .Cout(n1b_alu_8_cout), .A_prime(A_prime),
    .B_prime(B_prime), .out_8(out_7[7]));  // open: Set
  _1b_ALU u_1b_alu_9 (
    .A(A[8]), .B(B[8]), .Less(1'b0), .Cin(n1b_alu_8_cout), .Op(Op), .Cout(n1b_alu_9_cout), .A_prime(A_prime),
    .B_prime(B_prime), .out_8(out_7[8]));  // open: Set
  _1b_ALU u_1b_alu_10 (
    .A(A[9]), .B(B[9]), .Less(1'b0), .Cin(n1b_alu_9_cout), .Op(Op), .Cout(n1b_alu_10_cout),
    .A_prime(A_prime), .B_prime(B_prime), .out_8(out_7[9]));  // open: Set
  _1b_ALU u_1b_alu_11 (
    .A(A[10]), .B(B[10]), .Less(1'b0), .Cin(n1b_alu_10_cout), .Op(Op), .Cout(n1b_alu_11_cout),
    .A_prime(A_prime), .B_prime(B_prime), .out_8(out_7[10]));  // open: Set
  _1b_ALU u_1b_alu_12 (
    .A(A[11]), .B(B_prime), .Less(1'b0), .Cin(n1b_alu_11_cout), .Op(Op), .Cout(n1b_alu_12_cout),
    .A_prime(A_prime), .B_prime(B[11]), .out_8(out_7[11]));  // open: Set
  _1b_ALU u_1b_alu_13 (
    .A(A[12]), .B(B[12]), .Less(1'b0), .Cin(n1b_alu_12_cout), .Op(Op), .Cout(n1b_alu_13_cout),
    .A_prime(A_prime), .B_prime(B_prime), .out_8(out_7[12]));  // open: Set
  _1b_ALU u_1b_alu_14 (
    .A(A[13]), .B(B[13]), .Less(1'b0), .Cin(n1b_alu_13_cout), .Op(Op), .Cout(n1b_alu_14_cout),
    .A_prime(A_prime), .B_prime(B_prime), .out_8(out_7[13]));  // open: Set
  _1b_ALU u_1b_alu_15 (
    .A(A[14]), .B(B[14]), .Less(1'b0), .Cin(n1b_alu_14_cout), .Op(Op), .Cout(n1b_alu_15_cout),
    .A_prime(A_prime), .B_prime(B_prime), .out_8(out_7[14]));  // open: Set
  _1b_ALU u_1b_alu_16 (
    .A(A[15]), .B(B[15]), .Less(1'b0), .Cin(n1b_alu_15_cout), .Op(Op), .Set(n1b_alu_16_set),
    .A_prime(A_prime), .B_prime(B_prime), .out_8(out_7[15]));  // open: Cout
  nor nor_1 (Zero, out_7[0], out_7[1], out_7[2], out_7[3], out_7[4], out_7[5], out_7[6], out_7[7], out_7[8], out_7[9], out_7[10], out_7[11], out_7[12], out_7[13], out_7[14], out_7[15]);
endmodule

module project (
  input  [1:0] Op,
  input  Cin,
  input  [15:0] A,
  input  A_prime,
  input  [15:0] B,
  input  B_prime,
  output [15:0] result,
  output Zero
);

  ALU alu_1 (.A_prime(A_prime), .B_prime(B_prime), .out_7(result), .Zero(Zero), .B(B), .A(A), .Cin(Cin), .Op(Op));
endmodule

module ALU_16b (
  input  [1:0] Op_code,
  input  Cin,
  input  [15:0] A,
  input  A_prime,
  input  [15:0] B,
  input  B_prime,
  output [15:0] Result,
  output Zero
);

  ALU alu_1 (.A_prime(A_prime), .B_prime(B_prime), .out_7(Result), .Zero(Zero), .B(B), .A(A), .Cin(Cin), .Op(Op_code));
endmodule
