// Logisim project Control_Unit.circ as structural Verilog: 1 circuit, main circuit main
module main (
  input  Op_5,
  input  Op_4,
  input  Op_3,
  input  Op_2,
  input  Op_1,
  input  Op_0,
  output RegDst,
  output ALU_Src,
  output Mem_to_Reg,
  output Reg_write,
  output Mem_read,
  output Mem_Write,
  output Branch,
  output ALU0P0,
  output ALUOP1,
  output lhu
);

  wire lw_out;

  and R_format (ALU0P0, ~Op_5, ~Op_4, ~Op_3, ~Op_2, ~Op_1, ~Op_0);  // AND_Gate
  and lw (lw_out, Op_5, ~Op_4, ~Op_3, ~Op_2, Op_1, Op_0);  // AND_Gate
  and sw (Mem_Write, Op_5, ~Op_4, Op_3, ~Op_2, Op_1, Op_0);  // AND_Gate
  and beq (ALUOP1, ~Op_5, ~Op_4, ~Op_3, Op_2, ~Op_1, ~Op_0);  // AND_Gate
  and u_Lhu (lhu, Op_5, ~Op_4, ~Op_3, Op_2, ~Op_1, Op_0);  // AND_Gate
  or or_1 (ALU_Src, Mem_Write, lhu, lw_out);
  or or_2 (Mem_to_Reg, lhu, lw_out);
  or or_3 (Reg_write, lw_out, lhu, ALU0P0);
  or or_4 (Mem_read, lhu, lw_out);

  assign Branch = ALUOP1;
  assign RegDst = ALU0P0;

  // Notes on the sheet:
  //   25 hex = 37
  //   load half unsind
  //   op : 100101
endmodule
